# Fritzing sketch esquema_pictorico (saved by Fritzing 0.9.5d)
breadboards: 1

parts:
  Componente1 = Barometric Pressure Sensor - BMP180 Breakout (GY-68)
  DHT1 = Humidity and Temperature Sensor DHT11
  Componente2 = Arduino Uno (Rev3)
  R1 = Resistor [tolerance=±5% resistance=4700 package=THT]

nets:
  VCC: Componente1.VCC, DHT1.Vcc, Componente2.5V, R1.Pin_1
  GND: Componente1.GND, DHT1.GND_2, Componente2.GND
  N1: Componente1.SCL, Componente2.A5/SCL
  N2: Componente1.SDA, Componente2.A4/SDA
  N3: DHT1.Data-signal, Componente2.D2, R1.Pin_0

custom parts:
  Humidity and Temperature Sensor DHT11: Digital relative humidity & temperature sensor DHT11
